# Fritzing sketch brs_2 (saved by Fritzing 0.9.1b)
breadboards: 1

parts:
  Part6 = Arduino Uno (Rev3)
  VCC1 = Battery block 9V
  Part7 = SRF05 Ultrasonic Rangefinder
  Part8 = SRF05 Ultrasonic Rangefinder
  Part9 = SRF05 Ultrasonic Rangefinder

nets:
  N1: Part6.D8, Part9.Trig
  N2: Part6.D9_PWM, Part9.Echo
  GND: Part6.GND, Part7.GND, Part8.GND, Part9.GND
  N3: Part6.D4, Part7.Trig
  N4: Part6.D5_PWM, Part7.Echo
  N5: Part6.D6_PWM, Part8.Trig
  N6: Part6.D7, Part8.Echo
  VCC: Part6.5V, Part7.VCC, Part8.VCC, Part9.VCC
  N7: Part6.VIN, VCC1.-
