# Fritzing sketch brs (saved by Fritzing 0.9.1b)
breadboards: 1

parts:
  Part1 = Arduino Uno (Rev3)
  Part3 = SRF05 Ultrasonic Rangefinder
  Part4 = SRF05 Ultrasonic Rangefinder
  Part5 = SRF05 Ultrasonic Rangefinder
  Part6 = SRF05 Ultrasonic Rangefinder
  Part7 = SRF05 Ultrasonic Rangefinder
  VCC1 = Battery block 9V

nets:
  N1: Part1.D8, Part4.Echo
  N2: Part1.D9_PWM, Part4.Trig
  N3: Part1.D10_PWM/SS, Part6.Echo
  N4: Part1.D11_PWM/MOSI, Part6.Trig
  N5: Part1.D2, Part7.Trig
  N6: Part1.D3_PWM, Part7.Echo
  N7: Part1.D4, Part5.Echo
  N8: Part1.D5_PWM, Part5.Trig
  N9: Part1.D6_PWM, Part3.Trig
  N10: Part1.D7, Part3.Echo
  VCC: Part1.5V, Part3.VCC, Part4.VCC, Part5.VCC, Part6.VCC, Part7.VCC
  GND: Part1.GND, Part3.GND, Part4.GND, Part5.GND, Part6.GND, Part7.GND, VCC1.-
  N11: Part1.VIN, VCC1.+
